# Fritzing sketch MotorSchematic (saved by Fritzing 0.9.1b)
breadboards: 1

parts:
  Raspberry_Pi1 = Raspberry Pi B rev2
  IC1 = L293D [package=THT]
  M1 = DC Motor
  M2 = DC Motor
  VCC1 = Battery
  R1 = Resistor [tolerance=±5% resistance=220 package=THT]
  LED1 = LED - 5mm [color="Red (633nm)" package="5 mm [THT]"]
  Part1 = Thumb Joystick
  IC2 = MCP3008 8-channel 10-bit ADC [part_number=MCP3008]

nets:
  5V: Raspberry_Pi1.5V, IC1.+V, Part1.VCC, IC2.no_name_yet#15, IC2.no_name_yet#16
  GND: Raspberry_Pi1.GND, IC1.0V, VCC1.-, LED1.cathode, Part1.GND, IC2.no_name_yet#9, IC2.no_name_yet#14
  N1: Raspberry_Pi1.GPIO_23, IC1.Enable_2
  N2: Raspberry_Pi1.GPIO_14, IC1.Enable_1
  N3: Raspberry_Pi1.GPIO_15, IC1.In_1
  N4: Raspberry_Pi1.GPIO_18, IC1.In_2
  N5: Raspberry_Pi1.GPIO_4, R1.Pin_0
  N6: Raspberry_Pi1.GPIO_24, IC1.In_3
  N7: Raspberry_Pi1.GPIO_10, IC2.no_name_yet#11
  N8: Raspberry_Pi1.GPIO_9, IC2.no_name_yet#12
  N9: Raspberry_Pi1.GPIO_25, IC1.In_4
  N10: Raspberry_Pi1.GPIO_11, IC2.no_name_yet#13
  N11: Raspberry_Pi1.GPIO_8, IC2.no_name_yet#10
  N12: IC1.Out_1_(_Controlled_by_Enable_1_), M1.pin_2
  N13: IC1.Out_2_(_Controlled_by_Enable_1_), M1.pin_1
  N14: IC1.+Vmotor, VCC1.+
  N15: IC1.Out_3_(_Controlled_by_Enable_2_), M2.pin_2
  N16: IC1.Out_4_(_Controlled_by_Enable_2_), M2.pin_1
  N17: R1.Pin_1, LED1.anode
  N18: Part1.HORZ, IC2.no_name_yet#1
